# Fritzing sketch wiring-distance (saved by Fritzing 1.0.8)
breadboards: 1

parts:
  A1 = Arduino UNO R4 WiFi
  LED1 = LED - 5mm [color="Red (633nm)" current=0.030A package="5 mm [THT]"]
  R2 = Resistor [tolerance=±5% power=0.25W resistance=47 package=THT]
  HC-SR04_Sensor_1 = HC-SR04 Ultrasonic Distance Sensor

nets:
  N1: A1.Pin_2, A1.Pin_10, R2.Pin_0, HC-SR04_Sensor_1.GND
  N2: A1.Pin_8, HC-SR04_Sensor_1.VCC
  N3: A1.Pin_41, HC-SR04_Sensor_1.TRIG
  N4: A1.Pin_42, HC-SR04_Sensor_1.ECHO
  N5: A1.Pin_43, LED1.anode
  N6: LED1.cathode, R2.Pin_1

custom parts:
  Arduino UNO R4 WiFi: The Arduino UNO R4 WiFi merges the RA4M1 microprocessor from Renesas with the ESP32-S3 from Espressif, creating an all-in-one tool for makers with enhanced processing power and a diverse array of new peripherals.
