# Fritzing sketch wiring-led4 (saved by Fritzing 1.0.8)
breadboards: 1

parts:
  A1 = Arduino UNO R4 WiFi
  R2 = Resistor [tolerance=±5% power=0.25W resistance=47 package=THT]
  LED2 = RGB LED (com. anode, rbg) [color="Red (633nm)" current=0.030A package="5 mm [THT]"]
  R3 = Resistor [tolerance=±5% power=0.25W resistance=47 package=THT]
  R4 = Resistor [tolerance=±5% power=0.25W resistance=47 package=THT]

nets:
  N1: A1.Pin_2, A1.Pin_10, A1.Pin_30, LED2.common_anode
  N2: A1.Pin_43, R2.Pin_0
  N3: A1.Pin_44, R3.Pin_0
  N4: A1.Pin_45, R4.Pin_0
  N5: R2.Pin_1, LED2.red_cathode
  N6: LED2.blue_cathode, R3.Pin_1
  N7: LED2.green_cathode, R4.Pin_1

custom parts:
  Arduino UNO R4 WiFi: The Arduino UNO R4 WiFi merges the RA4M1 microprocessor from Renesas with the ESP32-S3 from Espressif, creating an all-in-one tool for makers with enhanced processing power and a diverse array of new peripherals.
