# Fritzing sketch wiring-photoresistor (saved by Fritzing 1.0.8)
breadboards: 1

parts:
  A1 = Arduino UNO R4 WiFi
  LED1 = LED - 5mm [color="Red (633nm)" current=0.030A package="5 mm [THT]"]
  R2 = Resistor [tolerance=±5% power=0.25W resistance=47 package=THT]
  R3 = Photocell (LDR) [power=0.25W dark_resistance_@0.01lx=300kΩ light_resistance_@100lx=400Ω luminance=10lx package=THT]
  R4 = Resistor [tolerance=±5% power=0.25W resistance=10k package=THT]

nets:
  N1: A1.Pin_2, A1.Pin_10, R2.Pin_0, R4.Pin_0
  N2: A1.Pin_8, R3.pin_0
  N3: A1.Pin_12, R3.pin_1, R4.Pin_1
  N4: A1.Pin_43, LED1.anode
  N5: LED1.cathode, R2.Pin_1

custom parts:
  Arduino UNO R4 WiFi: The Arduino UNO R4 WiFi merges the RA4M1 microprocessor from Renesas with the ESP32-S3 from Espressif, creating an all-in-one tool for makers with enhanced processing power and a diverse array of new peripherals.
