# Fritzing sketch wiring-pot (saved by Fritzing 1.0.8)
breadboards: 1

parts:
  A1 = Arduino UNO R4 WiFi
  LED1 = LED - 5mm [color="Red (633nm)" current=0.030A package="5 mm [THT]"]
  R2 = Resistor [tolerance=±5% power=0.25W resistance=47 package=THT]
  R1 = 6mm Trimmer Potentiometer [maximum_resistance=10kΩ knob_status=50% power=0.5W package=THT]

nets:
  N1: A1.Pin_2, A1.Pin_10, A1.Pin_30, R2.Pin_0, R1.leg1
  N2: A1.Pin_8, R1.leg2
  N3: A1.Pin_12, R1.wiper
  N4: A1.Pin_43, LED1.anode
  N5: LED1.cathode, R2.Pin_1

custom parts:
  Arduino UNO R4 WiFi: The Arduino UNO R4 WiFi merges the RA4M1 microprocessor from Renesas with the ESP32-S3 from Espressif, creating an all-in-one tool for makers with enhanced processing power and a diverse array of new peripherals.
