# Fritzing sketch wiring-stepper (saved by Fritzing 1.0.8)
breadboards: 1

parts:
  A1 = Arduino UNO R4 WiFi
  R1 = 6mm Trimmer Potentiometer [maximum_resistance=10kΩ knob_status=50% power=0.5W package=THT]
  Driver2 = 28BYJ-48 Driver Module [part_number=ULN2003 package=THT]
  SM2 = 28BYJ-48 Stepper Motor [part_number=28BYJ-48]

nets:
  N1: A1.Pin_2, A1.Pin_9, A1.Pin_10, R1.leg1, Driver2.GND
  N2: A1.Pin_8, R1.leg2, Driver2.Vmotor
  N3: A1.Pin_12, R1.wiper
  N4: A1.Pin_42, Driver2.IN1
  N5: A1.Pin_43, Driver2.IN2
  N6: A1.Pin_44, Driver2.IN3
  N7: A1.Pin_45, Driver2.IN4
  N8: Driver2.blue-pin, SM2.blue-pin
  N9: Driver2.pink-pin, SM2.pink-pin
  N10: Driver2.yellow-pin, SM2.yellow-pin
  N11: Driver2.orange-pin, SM2.orange-pin
  N12: Driver2.red-pin, SM2.red-pin

custom parts:
  Arduino UNO R4 WiFi: The Arduino UNO R4 WiFi merges the RA4M1 microprocessor from Renesas with the ESP32-S3 from Espressif, creating an all-in-one tool for makers with enhanced processing power and a diverse array of new peripherals.
  28BYJ-48 Driver Module: ULN2003 Driver Module for the 28BYJ-48 Unipolar Stepper Motor LED A - Blue wire - Bottom coil left LED B - Pink wire - Top coil left LED C - Yellow wire - Bottom coil right LED D - Orange wire - Top coil right Common rail - red Connector pins: blue - pink - yellow - orange - red Control pins - IN1 to IN4 Power pins - GND & Vmotor (5-12V) On/Off jumper (if removed, power to motor is cut).
  28BYJ-48 Stepper Motor: Unipolar Stepper Motor 28BYJ-48 Top coil - pink & orange Bottom coil - blue & yellow Common rail - red Connector pins: blue - pink - yellow - orange - red
